# Fritzing sketch lcd_i2c (saved by Fritzing 0.9.2b)

parts:
  LCD1 = LCD screen  # not connected
  Part1 = Spark Core (v1.0)
  J1 = screw terminal, 4 pins
  R1 = Resistor [tolerance=±5% resistance=4.7k package="0402 [SMD]"]
  R2 = Resistor [tolerance=±5% resistance=4.7k package="0402 [SMD]"]

nets:
  N1: Part1.GND, J1.pin1
  N2: Part1.VIN, J1.pin2, R1.Pin_0, R2.Pin_0
  N3: Part1.D0, J1.pin3
  N4: Part1.D1, J1.pin4

notes:
  LCD Backpack
  GND
  VCC
  SDA
  SCL
  The pullup resistors should not be necessary for most backpacks since they should be integrated there.
